// Logisim project lab2.circ as structural Verilog: 1 circuit, main circuit main
module main (
  input  O2,
  input  A0,
  input  O1,
  input  B0,
  input  O0,
  input  A1,
  input  B1,
  output L0,
  output L1,
  output L2,
  output L3,
  output L4,
  output L5,
  output L6,
  output L7,
  output S
);

  wire and_1_out, and_2_out, and_3_out, and_4_out, and_5_out, and_6_out, and_7_out, and_8_out, and_9_out,
       and_10_out, and_11_out, and_12_out, and_13_out, n3_to_8_decoder_74138_1_p9,
       n3_to_8_decoder_74138_1_p10, n3_to_8_decoder_74138_2_p7, n3_to_8_decoder_74138_2_p8,
       n3_to_8_decoder_74138_2_p9, n3_to_8_decoder_74138_2_p10, n3_to_8_decoder_74138_2_p11,
       n3_to_8_decoder_74138_2_p12, n3_to_8_decoder_74138_2_p13, n3_to_8_decoder_74138_2_p14,
       n4_to_1_mux_x2_74153_1_p13, n4_to_1_mux_x2_74153_1_p14, n4_to_1_mux_x2_74153_2_p11,
       n4_to_1_mux_x2_74153_2_p12, not_1_out, not_2_out, not_3_out, not_4_out, not_5_out, not_6_out,
       not_7_out, not_8_out, not_9_out, not_10_out, not_11_out, not_12_out, not_13_out, not_14_out, or_1_out,
       or_2_out, or_3_out, or_4_out, or_5_out, or_6_out, or_7_out, or_8_out, or_9_out, or_10_out, xor_1_out,
       xor_2_out, xor_3_out;

  or or_1 (or_1_out, A1, B1);
  and and_1 (and_1_out, A1, B1);
  xor xor_1 (xor_1_out, A1, B1);
  or or_2 (or_2_out, A0, B0);
  and and_2 (and_2_out, A0, B0);
  xor xor_2 (xor_2_out, A0, B0);
  not not_1 (not_1_out, A0);
  not not_2 (not_2_out, A1);
  and and_3 (and_3_out, not_2_out, B1);
  and and_4 (and_4_out, and_2_out, or_1_out);
  not not_3 (not_3_out, A1);
  not not_4 (not_4_out, A0);
  not not_5 (not_5_out, B1);
  and and_5 (and_5_out, not_5_out, A1);
  or or_3 (or_3_out, A0, not_6_out);
  not not_6 (not_6_out, B0);
  and and_6 (and_6_out, not_1_out, B0);
  or or_4 (or_4_out, not_2_out, B1);
  not not_7 (not_7_out, xor_2_out);
  not not_8 (not_8_out, xor_1_out);
  xor xor_3 (xor_3_out, xor_1_out, and_2_out);
  and and_7 (and_7_out, not_3_out, B1);
  or or_5 (or_5_out, and_2_out, not_4_out);
  and and_8 (and_8_out, and_5_out, or_3_out);
  and and_9 (and_9_out, and_6_out, or_4_out);
  or or_6 (or_6_out, and_9_out, and_3_out);
  not not_9 (not_9_out, or_2_out);
  not not_10 (not_10_out, or_1_out);
  and and_10 (and_10_out, not_7_out, not_8_out);
  or or_7 (or_7_out, and_1_out, and_4_out);
  and and_11 (and_11_out, and_7_out, or_5_out);
  or or_8 (or_8_out, and_11_out, and_8_out);
  and and_12 (and_12_out, or_8_out, not_13_out);
  // _3_to_8_decoder__74138 #(.Facing("east")) 3_to_8_decoder_74138_1: pin names not known; wires that end beside it: O0, O1, O2, 1'b1, 1'b0, 1'b0, O0, O1, n3_to_8_decoder_74138_1_p9, n3_to_8_decoder_74138_1_p10
  not not_11 (not_11_out, O2);
  // _4_to_1_MUX__x2___74153 #(.Facing("east")) 4_to_1_mux_x2_74153_1: pin names not known; wires that end beside it: or_2_out, and_2_out, not_9_out, xor_2_out, xor_2_out, xor_2_out, and_10_out, 1'b0, O2, O0, not_11_out, O1, n4_to_1_mux_x2_74153_1_p13, n4_to_1_mux_x2_74153_1_p14
  not not_12 (not_12_out, O2);
  // _4_to_1_MUX__x2___74153 #(.Facing("east")) 4_to_1_mux_x2_74153_2: pin names not known; wires that end beside it: or_1_out, and_1_out, not_10_out, xor_1_out, and_12_out, xor_3_out, 1'b0, 1'b0, O2, not_12_out, n4_to_1_mux_x2_74153_2_p11, n4_to_1_mux_x2_74153_2_p12
  not not_13 (not_13_out, n3_to_8_decoder_74138_1_p9);
  or or_9 (or_9_out, n4_to_1_mux_x2_74153_1_p13, n4_to_1_mux_x2_74153_1_p14);
  or or_10 (or_10_out, n4_to_1_mux_x2_74153_2_p11, n4_to_1_mux_x2_74153_2_p12);
  not not_14 (not_14_out, n3_to_8_decoder_74138_1_p10);
  and and_13 (and_13_out, not_14_out, or_7_out);
  and and_14 (S, not_13_out, or_6_out);
  // _3_to_8_decoder__74138 #(.Facing("east")) 3_to_8_decoder_74138_2: pin names not known; wires that end beside it: or_9_out, or_10_out, and_13_out, 1'b1, 1'b0, 1'b0, n3_to_8_decoder_74138_2_p7, n3_to_8_decoder_74138_2_p8, n3_to_8_decoder_74138_2_p9, n3_to_8_decoder_74138_2_p10, n3_to_8_decoder_74138_2_p11, n3_to_8_decoder_74138_2_p12, n3_to_8_decoder_74138_2_p13, n3_to_8_decoder_74138_2_p14
  not not_15 (L0, n3_to_8_decoder_74138_2_p7);
  not not_16 (L1, n3_to_8_decoder_74138_2_p8);
  not not_17 (L2, n3_to_8_decoder_74138_2_p9);
  not not_18 (L3, n3_to_8_decoder_74138_2_p10);
  not not_19 (L4, n3_to_8_decoder_74138_2_p11);
  not not_20 (L5, n3_to_8_decoder_74138_2_p12);
  not not_21 (L6, n3_to_8_decoder_74138_2_p13);
  not not_22 (L7, n3_to_8_decoder_74138_2_p14);
endmodule
