// Logisim project demux.circ as structural Verilog: 1 circuit, main circuit main
module main (
  input  I0,
  input  S1,
  input  S0,
  output O3,
  output O2,
  output O1,
  output O0
);

  wire and_1_out, and_2_out, and_3_out, and_4_out, controlled_buffer_1_out, controlled_buffer_2_out,
       controlled_buffer_3_out, controlled_buffer_4_out, not_1_out, not_2_out, not_3_out, not_4_out;

  not not_1 (not_1_out, S1);
  not not_2 (not_2_out, S0);
  not not_3 (not_3_out, S1);
  and and_1 (and_1_out, not_1_out, not_2_out);
  not not_4 (not_4_out, S0);
  and and_2 (and_2_out, not_3_out, S0);
  and and_3 (and_3_out, S1, S0);
  and and_4 (and_4_out, S1, not_4_out);
  assign controlled_buffer_1_out = and_2_out ? I0 : 1'bz;  // Controlled_Buffer controlled_buffer_1
  assign controlled_buffer_2_out = and_1_out ? I0 : 1'bz;  // Controlled_Buffer controlled_buffer_2
  assign controlled_buffer_3_out = and_3_out ? I0 : 1'bz;  // Controlled_Buffer controlled_buffer_3
  assign controlled_buffer_4_out = and_4_out ? I0 : 1'bz;  // Controlled_Buffer controlled_buffer_4
  and and_5 (O3, controlled_buffer_3_out, and_3_out);
  and and_6 (O2, controlled_buffer_4_out, and_4_out);
  and and_7 (O1, controlled_buffer_1_out, and_2_out);
  and and_8 (O0, controlled_buffer_2_out, and_1_out);
endmodule
