// Logisim project encoder.circ as structural Verilog: 1 circuit, main circuit main
module main (
  input  I0,
  input  I1,
  input  I2,
  input  I3,
  output O0,
  output O1
);

  or or_1 (O0, I1, I3);
  or or_2 (O1, I3, I2);
endmodule
