// Logisim project register.circ as structural Verilog: 1 circuit, main circuit main
module main (
  input  CLK,
  input  D,
  input  A0,
  input  A1,
  input  A2,
  output Bit4,
  output Bit0,
  output Bit5,
  output Bit1,
  output Bit6,
  output Bit2,
  output Bit7,
  output Bit3
);

  wire and_1_out, and_2_out, and_3_out, and_4_out, dual_d_flip_flop_7474_1_p8, dual_d_flip_flop_7474_2_p8,
       dual_d_flip_flop_7474_3_p8, dual_d_flip_flop_7474_4_p8, n3_to_8_decoder_74138_1_p7,
       n3_to_8_decoder_74138_1_p8, n3_to_8_decoder_74138_1_p9, n3_to_8_decoder_74138_1_p10,
       n3_to_8_decoder_74138_1_p11, n3_to_8_decoder_74138_1_p12, n3_to_8_decoder_74138_1_p13,
       n3_to_8_decoder_74138_1_p14, not_1_out, not_2_out, not_3_out, not_4_out, not_5_out, not_6_out,
       not_7_out, not_8_out;

  // _3_to_8_decoder__74138 #(.Facing("east")) 3_to_8_decoder_74138_1: pin names not known; wires that end beside it: A0, A1, A2, 1'b1, 1'b0, 1'b0, n3_to_8_decoder_74138_1_p7, n3_to_8_decoder_74138_1_p8, n3_to_8_decoder_74138_1_p9, n3_to_8_decoder_74138_1_p10, n3_to_8_decoder_74138_1_p11, n3_to_8_decoder_74138_1_p12, n3_to_8_decoder_74138_1_p13, n3_to_8_decoder_74138_1_p14
  not not_1 (not_1_out, n3_to_8_decoder_74138_1_p7);
  not not_2 (not_2_out, n3_to_8_decoder_74138_1_p8);
  not not_3 (not_3_out, n3_to_8_decoder_74138_1_p9);
  not not_4 (not_4_out, n3_to_8_decoder_74138_1_p10);
  not not_5 (not_5_out, n3_to_8_decoder_74138_1_p11);
  not not_6 (not_6_out, n3_to_8_decoder_74138_1_p12);
  not not_7 (not_7_out, n3_to_8_decoder_74138_1_p13);
  not not_8 (not_8_out, n3_to_8_decoder_74138_1_p14);
  and and_1 (and_1_out, not_5_out, CLK);
  and and_2 (and_2_out, not_6_out, CLK);
  and and_3 (and_3_out, not_7_out, CLK);
  and and_4 (and_4_out, not_8_out, CLK);
  // Dual_D_Flip_Flop__7474 #(.Facing("east")) dual_d_flip_flop_7474_1: pin names not known; wires that end beside it: 1'b1, D, and_1_out, 1'b1, Bit4, 1'b1, D, dual_d_flip_flop_7474_1_p8, 1'b1, Bit0
  // Dual_D_Flip_Flop__7474 #(.Facing("east")) dual_d_flip_flop_7474_2: pin names not known; wires that end beside it: 1'b1, D, and_2_out, 1'b1, Bit5, 1'b1, D, dual_d_flip_flop_7474_2_p8, 1'b1, Bit1
  // Dual_D_Flip_Flop__7474 #(.Facing("east")) dual_d_flip_flop_7474_3: pin names not known; wires that end beside it: 1'b1, D, and_3_out, 1'b1, Bit6, 1'b1, D, dual_d_flip_flop_7474_3_p8, 1'b1, Bit2
  // Dual_D_Flip_Flop__7474 #(.Facing("east")) dual_d_flip_flop_7474_4: pin names not known; wires that end beside it: 1'b1, D, and_4_out, 1'b1, Bit7, 1'b1, D, dual_d_flip_flop_7474_4_p8, 1'b1, Bit3
  and and_5 (dual_d_flip_flop_7474_1_p8, not_1_out, CLK);
  and and_6 (dual_d_flip_flop_7474_2_p8, not_2_out, CLK);
  and and_7 (dual_d_flip_flop_7474_3_p8, not_3_out, CLK);
  and and_8 (dual_d_flip_flop_7474_4_p8, not_4_out, CLK);
endmodule
